# Fritzing sketch Plan de montage (saved by Fritzing 0.9.2b)
breadboards: 1

parts:
  Composant1 = LIDAR-Lite
  Raspberry_Pi1 = Raspberry Pi 2
  U1 = mystery part, 6 pins [chip_label=Stepper01]
  U2 = mystery part, 6 pins [chip_label="Stepper 02"]
  S1 = Pushbutton [package="[THT]"]
  S2 = Pushbutton [package="[SMD]"]

nets:
  5V: Composant1.5V, Raspberry_Pi1.5V, U1.pin5, U2.pin5
  N1: Composant1.SCL, Raspberry_Pi1.GPIO3
  N2: Composant1.SDA, Raspberry_Pi1.GPIO2
  GND: Composant1.GND, Raspberry_Pi1.GND, U1.pin6, U2.pin6
  N3: Raspberry_Pi1.GPIO22, Raspberry_Pi1.3V3, Raspberry_Pi1.GPIO23, S1.Pin_1, S1.Pin_2, S2.Pin_3, S2.Pin_4
  N4: Raspberry_Pi1.GPIO6, U2.pin1
  N5: Raspberry_Pi1.GPIO13, U2.pin2
  N6: Raspberry_Pi1.GPIO19, U2.pin3
  N7: Raspberry_Pi1.GPIO26, U2.pin4
  N8: Raspberry_Pi1.GPIO21, U1.pin4
  N9: Raspberry_Pi1.GPIO20, U1.pin3
  N10: Raspberry_Pi1.GPIO16, U1.pin2
  N11: Raspberry_Pi1.GPIO12, U1.pin1
  N12: S1.Pin_3, S1.Pin_4
  N13: S2.Pin_1, S2.Pin_2

custom parts:
  LIDAR-Lite: PulsedLight LIDAR-Lite Sensor
